# Fritzing sketch Arduino_operator_NFC (saved by Fritzing 0.9.3b)

parts:
  Operator_Board_(Master) = Arduino Uno (Rev3)
  NFC_shield = Adafruit PN532 Breakout [part_number="Adafruit #364"]
  NFC_controller_(Slave) = Adafruit Feather 32u4 RFM69 433/900MHz

nets:
  N1: Operator_Board_(Master).A4/SDA, NFC_controller_(Slave).A4
  N2: Operator_Board_(Master).A5/SCL, NFC_controller_(Slave).A5
  3V3: Operator_Board_(Master).3V3, NFC_shield.VDD, NFC_controller_(Slave).+3V3
  GND: Operator_Board_(Master).GND, NFC_shield.GND, NFC_controller_(Slave).GND
  N3: NFC_shield.SCK, NFC_controller_(Slave).SCK
  N4: NFC_shield.MISO, NFC_controller_(Slave).MISO
  N5: NFC_shield.NSS/SCL/RX, NFC_controller_(Slave).5

custom parts:
  Adafruit PN532 Breakout: The PN532 is the most popular NFC chip, and is what is embedded in pretty much every phone or device that does NFC. It can pretty much do it all, such as read and write to tags and cards, communicate with phones (say for payment processing), and 'act' like a NFC tag. If you want to do any sort of embedded NFC work, this is the chip you'll want to use! NFC (Near Field Communications) is a way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
  Adafruit Feather 32u4 RFM69 433/900MHz: This is the Adafruit Feather 32u4 Radio (RFM69HCW) - our take on an microcontroller packet radio transceiver with built in USB and battery charging. Its an Adafruit Feather 32u4 with a 433 or 900 MHz radio module cooked in! Great for making wireless networks that can go further than 2.4GHz 802.15.4 and similar, are more flexible than Bluetooth LE and without the high power requirements of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
