# Fritzing sketch RaspPi_leds_and_lock (saved by Fritzing 0.9.0b)
breadboards: 1

parts:
  LED1 = LED - 5mm [color="Red (635nm)" package="5 mm [THT]"]
  LED2 = LED - 5mm [color="Green (555nm)" package="5 mm [THT]"]
  LED3 = LED - 5mm [color="Yellow (595nm)" package="5 mm [THT]"]
  R2 = Resistor [tolerance=±5% resistance=330 package="0805 [SMD]"]
  KY-1 = Keyes Relay [package=THT]
  (Solenoid) = Solenoid [part_number="Electric Strike Lock"]
  Raspberry_Pi_1 = Raspberry Pi 3 [part_number=RPI-3-V1.2]
  R1 = Resistor [tolerance=±5% resistance=330 package="0805 [SMD]"]
  R3 = Resistor [tolerance=±5% resistance=330 package="0805 [SMD]"]

nets:
  N1: LED1.cathode, Raspberry_Pi_1.GIPO17
  N2: LED1.anode, R1.Pin_1
  N3: LED2.cathode, Raspberry_Pi_1.GIPO22
  N4: LED2.anode, R3.Pin_1
  N5: LED3.cathode, Raspberry_Pi_1.GIPO27
  N6: LED3.anode, R2.Pin_1
  N7: R2.Pin_0, KY-1.ground, (Solenoid).pin1, Raspberry_Pi_1.GND, R1.Pin_0, R3.Pin_0
  N8: KY-1.signal, KY-1.C, Raspberry_Pi_1.GIPO4
  N9: KY-1.power, Raspberry_Pi_1.5V
  N10: KY-1.NC, (Solenoid).pin2

notes:
  --- WIRE KEY ---
  Black for Ground
  Red, yellow, green for LEDs
  Purple for relay power (5V)
  Cyan for relay signal (3.3V)
  12V power supply for strike lock necessary
  USB - to Arduino
  <- This is a generic solenoid part, not an actual strike lock

custom parts:
  Keyes Relay: The Keyes 5V relay module is suitable for SCM development, home appliance control. It uses a 5V~12V TIL control signal which can control DC / AC signal.
